# Fritzing sketch Circuit-wifi-ws2813 (saved by Fritzing 0.9.3b)

parts:
  U2 = ESP32S-HiLetgo [part_number=ESP32S-HiLetgo]
  D1 = Schottky Diode [part_number=1N5817 package="300 mil [THT]"]
  HLK-PM2 = HLK-PM01
  D3 = Diode [package=diode-1n4148]
  C7 = Tantalum Capacitor [capacitance=0.47mF package="200 mil [THT, tantalum]"]  # not connected
  WS1 = WS2813
  WS2813_Strip1 = WS2813 Strip
  WS2813_Strip2 = WS2813 Strip
  WS2813_Strip3 = WS2813 Strip
  WS2813_Strip4 = WS2813 Strip
  WS2813_Strip5 = WS2813 Strip
  D2 = Schottky Diode [part_number=1N5817 package="300 mil [THT]"]  # not connected
  C16 = Tantalum Capacitor [capacitance=0.47mF package="200 mil [THT, tantalum]"]
  C17 = Tantalum Capacitor [capacitance=0.47mF package="200 mil [THT, tantalum]"]
  C18 = Tantalum Capacitor [capacitance=0.47mF package="200 mil [THT, tantalum]"]
  C19 = Tantalum Capacitor [capacitance=0.47mF package="200 mil [THT, tantalum]"]
  R15 = Resistor [tolerance=±5% resistance=220 package=THT]
  R13 = Resistor [tolerance=±5% resistance=330 package=THT]
  R16 = Resistor [tolerance=±5% resistance=220 package="0402 [SMD]"]  # not connected
  U4 = MAX485 Breakout [chip_label=? package=THT]
  U5 = MAX485 Breakout [chip_label=? package=THT]
  U6 = MAX485 Breakout [chip_label=? package=THT]
  U7 = MAX485 Breakout [chip_label=? package=THT]
  R1 = Resistor [tolerance=±5% resistance=330 package=THT]
  R11 = Resistor [tolerance=±5% resistance=330 power=125mW package=THT]
  R18 = Resistor [tolerance=±5% resistance=330 package=THT]

nets:
  N1: U2.GPIO35, R1.Pin_0
  GND: U2.GND, D1.cathode, D1.anode, HLK-PM2.-Vo, WS1.GND
  N2: HLK-PM2.+Vo, D3.A, WS2813_Strip1.+5V
  N3: D3.C, WS1.+5V
  N4: WS1.DI, R1.Pin_1
  N5: WS1.DO, WS2813_Strip1.DI
  N6: WS1.BO, WS2813_Strip1.BI
  N7: WS2813_Strip1.DO, R18.Pin_0
  N8: WS2813_Strip1.BO, R11.Pin_0
  N9: WS2813_Strip2.BI, R11.Pin_1
  N10: WS2813_Strip2.DI, R18.Pin_1
  N11: WS2813_Strip2.+5V#3, C17.+
  N12: WS2813_Strip2.DO, U6.DI
  N13: WS2813_Strip3.BI, C18.-
  N14: WS2813_Strip3.DI, U7.RO
  N15: WS2813_Strip3.DO, R15.Pin_0
  N16: WS2813_Strip3.BO, R13.Pin_0
  N17: WS2813_Strip4.BI, R13.Pin_1
  N18: WS2813_Strip4.DI, R15.Pin_1
  N19: WS2813_Strip4.+5V#3, C19.+
  N20: WS2813_Strip4.DO, U4.DI
  N21: WS2813_Strip5.BI, C16.-
  N22: WS2813_Strip5.DI, U5.RO
  N23: WS2813_Strip5.+5V, C16.+
  N24: U4.B, U5.B
  N25: U4.A, U5.A
  N26: U6.B, U7.B
  N27: U6.A, U7.A

notes:
  Data+GND:
  Twisted pair,
  max 50 cm
  2x Twisted pair
  (DO+GND and BO+GND),
  max 50 cm
  Twisted pair,
  max 500 m
  > 1,5 mm^2 / AWG 15
  > 2,0 mm^2 / AWG 14 if longer than, say, 2m
  > 0,3 mm^2 / AWG 22
  Notes on MAX485
  Separate supply lines required as datasheet says +/- 5% stability required.
  Only data line realized with pairs of MAX485. Second pairs could be implemented for backup lines, but only of minor benefit.
  This ESP module has built in voltage regulator, it can be used on 5V.
  Protection circuit not working well with diode that creates the 4,3V supply for the first LED (1N4148). Could work, but maybe a separate level shifter is working better here.

custom parts:
  ESP32S-HiLetgo: HiLetgo ESP-WROOM-32 ESP32 ESP-32S Development Board 2.4GHz Dual-Mode WiFi + Bluetooth Dual Cores Microcontroller The ESP32 integrated with Antenna switches, RF Balun, power amplifiers, low-noise amplifiers, filters, and management modules, and the entire solution occupies the least area of PCB. 2.4 GHz Wi-Fi plus Bluetooth dual-mode chip, with TSMC Ultra-low power consumption 40nm technology,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
  WS2813: A single WS2813 LED on a short strip. Adapted from NeoPixel strips with 30 digitally-addressable pixel created by Dean Cording and John De Cristofaro.
  WS2813 Strip: WS2813 LED Strip Adapted from NeoPixel strips with 30 digitally-addressable pixel created by Dean Cording and John De Cristofaro.
  MAX485 Breakout: MAX485 RS485 breakout board
